// Logisim project 24125102_01.circ as structural Verilog: 3 circuits, main circuit main
module main (
  input  [3:0] A,
  input  [3:0] B,
  input  C,
  output [3:0] S,
  output hi
);

  wire full_adder_1_hi, full_adder_2_hi, full_adder_3_hi;

  full_adder full_adder_1 (.A(A[0]), .B(B[0]), .C(C), .lo(S[0]), .hi(full_adder_1_hi));
  full_adder full_adder_2 (.A(A[1]), .B(B[1]), .C(full_adder_1_hi), .lo(S[1]), .hi(full_adder_2_hi));
  full_adder full_adder_3 (.A(A[2]), .B(B[2]), .C(full_adder_2_hi), .lo(S[2]), .hi(full_adder_3_hi));
  full_adder full_adder_4 (.A(A[3]), .B(B[3]), .C(full_adder_3_hi), .lo(S[3]), .hi(hi));
endmodule

module full_adder (
  input  A,
  input  B,
  input  C,
  output lo,
  output hi
);

  wire half_adder_1_hi, half_adder_1_lo, half_adder_2_hi;

  half_adder half_adder_1 (.A(A), .B(B), .lo(half_adder_1_lo), .hi(half_adder_1_hi));
  half_adder half_adder_2 (.A(half_adder_1_lo), .B(C), .lo(lo), .hi(half_adder_2_hi));
  or or_1 (hi, half_adder_2_hi, half_adder_1_hi);
endmodule

module half_adder (
  input  A,
  input  B,
  output lo,
  output hi
);

  xor xor_1 (lo, A, B);
  and and_1 (hi, A, B);
endmodule
