// Logisim project 24125102_02.circ as structural Verilog: 3 circuits, main circuit main
module main (
  input  [7:0] A,
  input  [7:0] B,
  input  C,
  output [7:0] S,
  output hi
);

  wire full_adder_1_hi, full_adder_2_hi, full_adder_3_hi, full_adder_4_hi, full_adder_5_hi, full_adder_6_hi,
       full_adder_7_hi, full_adder_8_hi, not_2_out;
  wire [7:0] not_1_out;

  assign not_1_out = ~B;  // NOT_Gate not_1, 8 bits wide
  not not_2 (not_2_out, C);
  not not_3 (hi, full_adder_8_hi);
  full_adder full_adder_1 (.A(A[0]), .B(not_1_out[0]), .C(not_2_out), .lo(S[0]), .hi(full_adder_1_hi));
  full_adder full_adder_2 (.A(A[1]), .B(not_1_out[1]), .C(full_adder_1_hi), .lo(S[1]), .hi(full_adder_2_hi));
  full_adder full_adder_3 (.A(A[2]), .B(not_1_out[2]), .C(full_adder_2_hi), .lo(S[2]), .hi(full_adder_3_hi));
  full_adder full_adder_4 (.A(A[3]), .B(not_1_out[3]), .C(full_adder_3_hi), .lo(S[3]), .hi(full_adder_4_hi));
  full_adder full_adder_5 (.A(A[4]), .B(not_1_out[4]), .C(full_adder_4_hi), .lo(S[4]), .hi(full_adder_5_hi));
  full_adder full_adder_6 (.A(A[5]), .B(not_1_out[5]), .C(full_adder_5_hi), .lo(S[5]), .hi(full_adder_6_hi));
  full_adder full_adder_7 (.A(A[6]), .B(not_1_out[6]), .C(full_adder_6_hi), .lo(S[6]), .hi(full_adder_7_hi));
  full_adder full_adder_8 (.A(A[7]), .B(not_1_out[7]), .C(full_adder_7_hi), .lo(S[7]), .hi(full_adder_8_hi));
endmodule

module half_adder (
  input  A,
  input  B,
  output lo,
  output hi
);

  xor xor_1 (lo, A, B);
  and and_1 (hi, A, B);
endmodule

module full_adder (
  input  A,
  input  B,
  input  C,
  output lo,
  output hi
);

  wire half_adder_1_hi, half_adder_1_lo, half_adder_2_hi;

  half_adder half_adder_1 (.A(A), .B(B), .lo(half_adder_1_lo), .hi(half_adder_1_hi));
  half_adder half_adder_2 (.A(half_adder_1_lo), .B(C), .lo(lo), .hi(half_adder_2_hi));
  or or_1 (hi, half_adder_2_hi, half_adder_1_hi);
endmodule
