// Logisim project 24125102_03.circ as structural Verilog: 3 circuits, main circuit main
module main (
  input  [3:0] A,
  input  [3:0] B,
  input  Ctrl,
  input  C,
  output [3:0] S,
  output hi,
  output O
);

  wire full_adder_1_hi, full_adder_2_hi, full_adder_3_hi, full_adder_4_hi, xor_1_out, xor_2_out, xor_5_out,
       xor_6_out, xor_7_out;

  xor xor_1 (xor_1_out, Ctrl, B[0]);
  xor xor_2 (xor_2_out, C, Ctrl);
  xor xor_3 (hi, full_adder_4_hi, Ctrl);
  xor xor_4 (O, full_adder_3_hi, full_adder_4_hi);
  xor xor_5 (xor_5_out, Ctrl, B[1]);
  full_adder full_adder_1 (.A(A[0]), .B(xor_1_out), .C(xor_2_out), .lo(S[0]), .hi(full_adder_1_hi));
  xor xor_6 (xor_6_out, Ctrl, B[2]);
  full_adder full_adder_2 (.A(A[1]), .B(xor_5_out), .C(full_adder_1_hi), .lo(S[1]), .hi(full_adder_2_hi));
  full_adder full_adder_3 (.A(A[2]), .B(xor_6_out), .C(full_adder_2_hi), .lo(S[2]), .hi(full_adder_3_hi));
  xor xor_7 (xor_7_out, Ctrl, B[3]);
  full_adder full_adder_4 (.A(A[3]), .B(xor_7_out), .C(full_adder_3_hi), .lo(S[3]), .hi(full_adder_4_hi));
endmodule

module half_adder (
  input  A,
  input  B,
  output lo,
  output hi
);

  xor xor_1 (lo, A, B);
  and and_1 (hi, A, B);
endmodule

module full_adder (
  input  A,
  input  B,
  input  C,
  output lo,
  output hi
);

  wire half_adder_1_hi, half_adder_1_lo, half_adder_2_hi;

  half_adder half_adder_1 (.A(A), .B(B), .lo(half_adder_1_lo), .hi(half_adder_1_hi));
  half_adder half_adder_2 (.A(half_adder_1_lo), .B(C), .lo(lo), .hi(half_adder_2_hi));
  or or_1 (hi, half_adder_2_hi, half_adder_1_hi);
endmodule
